// Logisim project cpu.circ as structural Verilog: 2 circuits, main circuit main
module main (
  input  [31:0] INSTRUCTION,
  input  CLOCK,
  output [31:0] FETCH_ADDRESS,
  output [31:0] s0_Value,
  output [31:0] s1_Value,
  output [31:0] t0_Value,
  output [31:0] t1_Value,
  output [31:0] a0_Value,
  output [31:0] ra_Value,
  output [31:0] sp_Value
);

  wire Add, addASel, addBSel, Addi, addiASel, addiMemRW, addiPCSel, addMemRW, addPCSel, And, and_1_out,
       and_2_out, and_3_out, and_4_out, and_5_out, and_6_out, and_7_out, and_8_out, and_9_out, and_10_out,
       and_11_out, and_12_out, and_13_out, and_14_out, andASel, andBSel, Andi, andiASel, andiMemRW,
       andiPCSel, andMemRW, andPCSel, ASel, Beq, BeqMemRW, BeqRegWEn, Blt, BltMemRW, BltRegWEn, Bltu,
       BltuMemRW, BltuRegWEn, brEQ, brLT, BSel, comparator_1_eq, comparator_1_lt, comparator_2_eq,
       comparator_2_lt, Div, divASel, divBSel, divMemRW, divPCSel, Jal, JalMemRW, Jalr, JalrASel, JalrMemRW,
       Lb, lbASel, lbMemRW, lbPCSel, Lh, lhASel, lhMemRW, lhPCSel, Lui, LuiASel, LuiMemRW, LuiPCSel, Lw,
       lwASel, lwMemRW, lwPCSel, MEM_p1, MEM_p2, MEM_p4, MEM_p10, MemRW, Mul, mulASel, mulBSel, MulH,
       mulhASel, mulhBSel, mulhMemRW, mulhPCSel, mulMemRW, mulPCSel, NegSel, not_52_out, not_53_out,
       not_54_out, not_55_out, not_62_out, not_66_out, not_70_out, not_78_out, not_81_out, not_85_out,
       not_89_out, not_93_out, not_101_out, Or, or_1_out, or_2_out, or_3_out, or_4_out, or_5_out, or_6_out,
       or_7_out, or_8_out, or_9_out, or_10_out, or_11_out, or_12_out, or_13_out, orASel, orBSel, Ori,
       oriASel, oriMemRW, oriPCSel, orMemRW, orPCSel, PCSel, RegWEn, Rem, remASel, remBSel, remMemRW,
       remPCSel, Sll, sllASel, sllBSel, Slli, slliASel, slliMemRW, slliPCSel, sllMemRW, sllPCSel, Slt,
       sltASel, sltBSel, Slti, sltiASel, sltiMemRW, sltiPCSel, sltMemRW, sltPCSel, Srl, srlASel, srlBSel,
       Srli, srliASel, srliMemRW, srliPCSel, srlMemRW, srlPCSel, subASel, subBSel, subMemRW, subPCSel, Sw,
       SwASel, SwPCSel, SwRegWEn, Xor, xorASel, xorBSel, Xori, xoriASel, xoriMemRW, xoriPCSel, xorMemRW,
       xorPCSel;
  wire [1:0] addiWBSel, addWBSel, andiWBSel, andWBSel, BeqWBSel, BltuWBSel, BltWBSel, divWBSel, LuiWBSel,
       mulhWBSel, multiplexer_10_out, mulWBSel, oriWBSel, orWBSel, remWBSel, slliWBSel, sllWBSel, sltiWBSel,
       sltWBSel, srliWBSel, srlWBSel, subWBSel, SwWBSel, WBSel, xoriWBSel, xorWBSel;
  wire [2:0] addiImmSel, andiImmSel, ImmSel, JalrImmSel, lbImmSel, lhImmSel, lwImmSel, multiplexer_22_out,
       multiplexer_26_out, multiplexer_27_out, oriImmSel, slliImmSel, sltiImmSel, srliImmSel, xoriImmSel;
  wire [3:0] addALUSel, addiALUSel, ALUSel, BeqALUSel, bit_extender_1_out, bit_extender_4_out,
       bit_extender_19_out, bit_extender_30_out, bit_extender_36_out, bit_extender_38_out,
       bit_extender_39_out, bit_extender_42_out, bit_extender_44_out, bit_extender_45_out,
       bit_extender_47_out, bit_extender_50_out, bit_extender_52_out, BltALUSel, BltuALUSel, JalALUSel,
       JalrALUSel, lbALUSel, lhALUSel, LuiALUSel, lwALUSel, multiplexer_16_out, multiplexer_20_out,
       multiplexer_21_out, multiplexer_23_out, multiplexer_24_out, multiplexer_28_out, multiplexer_32_out,
       multiplexer_33_out, multiplexer_34_out, subALUSel, SwALUSel;
  wire [11:0] multiplexer_2_out, shifter_1_out;
  wire [12:0] shifter_3_out;
  wire [20:0] shifter_4_out;
  wire [24:0] Iimm, SBimm, Simm, Uimm, UJimm;
  wire [31:0] adder_1_out, bit_extender_15_out, bit_extender_16_out, bit_extender_17_out,
       bit_extender_18_out, bit_extender_40_out, bit_extender_41_out, demultiplexer_1_out0,
       demultiplexer_1_out1, demultiplexer_2_out0, demultiplexer_2_out1, immGen, Load, LoadOut,
       main_2_result, multiplexer_1_out, multiplexer_3_out, multiplexer_12_out, multiplexer_13_out,
       multiplexer_15_out, multiplexer_17_out, multiplexer_18_out, multiplexer_25_out, multiplexer_29_out,
       negator_1_out, prevPC, R1, R2, register_2_q, shifter_7_out, shifter_9_out;

  Multiplexer #(.width(32)) multiplexer_1 (
    .in0(adder_1_out), .in1(main_2_result), .out(multiplexer_1_out), .sel(PCSel));  // open: en
  Register #(.width(32)) PC (.D(multiplexer_1_out), .Q(FETCH_ADDRESS), .clk(CLOCK));  // open: en, clr
  Shifter #(.width(12), .shift("ar")) shifter_1 (.in(Iimm[24:13]), .\dist (4'b0010), .out(shifter_1_out));
  not not_1 (addPCSel, Add);
  not not_2 (addASel, Add);
  not not_3 (addBSel, Add);
  assign bit_extender_1_out = {{3{1'b0}}, Add};  // Bit_Extender bit_extender_1
  not not_4 (addMemRW, Add);
  assign addWBSel = {{1{1'b0}}, Add};  // Bit_Extender bit_extender_2
  not not_5 (mulPCSel, Mul);
  not not_6 (mulASel, Mul);
  not not_7 (mulBSel, Mul);
  not not_8 (mulMemRW, Mul);
  assign mulWBSel = {{1{1'b0}}, Mul};  // Bit_Extender bit_extender_3
  not not_9 (subPCSel, NegSel);
  not not_10 (subASel, NegSel);
  not not_11 (subBSel, NegSel);
  assign bit_extender_4_out = {{3{1'b0}}, NegSel};  // Bit_Extender bit_extender_4
  not not_12 (subMemRW, NegSel);
  assign subWBSel = {{1{1'b0}}, NegSel};  // Bit_Extender bit_extender_5
  not not_13 (sllPCSel, Sll);
  not not_14 (sllASel, Sll);
  not not_15 (sllBSel, Sll);
  not not_16 (sllMemRW, Sll);
  assign sllWBSel = {{1{1'b0}}, Sll};  // Bit_Extender bit_extender_6
  not not_17 (mulhPCSel, MulH);
  not not_18 (mulhASel, MulH);
  not not_19 (mulhBSel, MulH);
  not not_20 (mulhMemRW, MulH);
  assign mulhWBSel = {{1{1'b0}}, MulH};  // Bit_Extender bit_extender_7
  not not_21 (sltPCSel, Slt);
  not not_22 (sltASel, Slt);
  not not_23 (sltBSel, Slt);
  not not_24 (sltMemRW, Slt);
  assign sltWBSel = {{1{1'b0}}, Slt};  // Bit_Extender bit_extender_8
  not not_25 (xorPCSel, Xor);
  not not_26 (xorASel, Xor);
  not not_27 (xorBSel, Xor);
  not not_28 (xorMemRW, Xor);
  assign xorWBSel = {{1{1'b0}}, Xor};  // Bit_Extender bit_extender_9
  not not_29 (divPCSel, Div);
  not not_30 (divASel, Div);
  not not_31 (divBSel, Div);
  not not_32 (divMemRW, Div);
  assign divWBSel = {{1{1'b0}}, Div};  // Bit_Extender bit_extender_10
  not not_33 (srlPCSel, Srl);
  not not_34 (srlASel, Srl);
  not not_35 (srlBSel, Srl);
  not not_36 (srlMemRW, Srl);
  assign srlWBSel = {{1{1'b0}}, Srl};  // Bit_Extender bit_extender_11
  not not_37 (orPCSel, Or);
  not not_38 (orASel, Or);
  not not_39 (orBSel, Or);
  not not_40 (orMemRW, Or);
  assign orWBSel = {{1{1'b0}}, Or};  // Bit_Extender bit_extender_12
  not not_41 (remPCSel, Rem);
  not not_42 (remASel, Rem);
  not not_43 (remBSel, Rem);
  not not_44 (remMemRW, Rem);
  assign remWBSel = {{1{1'b0}}, Rem};  // Bit_Extender bit_extender_13
  not not_45 (andPCSel, And);
  not not_46 (andASel, And);
  not not_47 (andBSel, And);
  not not_48 (andMemRW, And);
  assign andWBSel = {{1{1'b0}}, And};  // Bit_Extender bit_extender_14
  Multiplexer #(.width(12)) multiplexer_2 (
    .in0(Iimm[24:13]), .in1(shifter_1_out), .out(multiplexer_2_out), .sel(Jalr));  // open: en
  Shifter #(.width(4)) shifter_2 (.in(bit_extender_1_out), .\dist (2'b01), .out(addALUSel));
  and and_1 (and_1_out, brEQ, Beq);
  Adder #(.width(32)) adder_1 (.a(FETCH_ADDRESS), .b(32'h1), .out(adder_1_out));  // open: cin, cout
  Multiplexer #(.width(32)) multiplexer_3 (
    .in0(INSTRUCTION), .in1({32{1'b0}}), .out(multiplexer_3_out), .sel(PCSel));  // open: en
  assign bit_extender_15_out = {{20{multiplexer_2_out[11]}}, multiplexer_2_out};  // Bit_Extender bit_extender_15
  assign bit_extender_16_out = {{20{Simm[24]}}, {Simm[24:18], Simm[4:0]}};  // Bit_Extender bit_extender_16
  assign bit_extender_17_out = {{19{shifter_3_out[12]}}, shifter_3_out};  // Bit_Extender bit_extender_17
  Shifter #(.width(13), .shift("ar")) shifter_3 (
    .in({SBimm[24], SBimm[0], SBimm[23:18], SBimm[4:1], 1'b0}), .\dist (4'b0010), .out(shifter_3_out));
  Shifter #(.width(21), .shift("ar")) shifter_4 (
    .in({UJimm[24], UJimm[12:5], UJimm[13], UJimm[23:14], 1'b0}), .\dist (5'b00010), .out(shifter_4_out));
  and and_2 (and_2_out, Blt, brLT);
  Register #(.width(32)) register_1 (.D(FETCH_ADDRESS), .Q(prevPC), .clk(CLOCK));  // open: en, clr
  Register #(.width(32)) register_2 (.D(multiplexer_3_out), .Q(register_2_q), .clk(CLOCK));  // open: en, clr
  assign bit_extender_18_out = {{11{shifter_4_out[20]}}, shifter_4_out};  // Bit_Extender bit_extender_18
  Demultiplexer #(.width(32)) demultiplexer_1 (
    .out0(demultiplexer_1_out0), .out1(demultiplexer_1_out1), .in(R1), .sel(Bltu));  // open: en
  Demultiplexer #(.width(32)) demultiplexer_2 (
    .out0(demultiplexer_2_out0), .out1(demultiplexer_2_out1), .in(R2), .sel(Bltu));  // open: en
  Shifter #(.width(4)) shifter_5 (.in(bit_extender_4_out), .\dist (2'b01), .out(subALUSel));
  Multiplexer multiplexer_4 (.in0(1'b0), .in1(1'b1), .out(PCSel), .sel(or_1_out));  // open: en
  or or_1 (or_1_out, and_1_out, and_2_out, and_3_out, Jal, Jalr);
  and and_3 (and_3_out, Bltu, brLT);
  Demultiplexer #(.select(3), .width(25)) demultiplexer_3 (
    .out0(Iimm), .out1(Simm), .out2(SBimm), .out3(Uimm), .out4(UJimm), .in(register_2_q[31:7]), .sel(ImmSel));  // open: out5, out6, out7, en
  Multiplexer #(.select(3), .width(32)) multiplexer_5 (
    .in0(bit_extender_15_out), .in1(bit_extender_16_out), .in2(bit_extender_17_out),
    .in3({Uimm[24:5], {12{1'b0}}}), .in4(bit_extender_18_out), .out(immGen), .sel(ImmSel));  // open: in5, in6, in7, en
  Comparator #(.width(32)) comparator_1 (
    .a(demultiplexer_1_out0), .b(demultiplexer_2_out0), .eq(comparator_1_eq), .lt(comparator_1_lt));  // open: gt
  Comparator #(.width(32), .mode("unsigned")) comparator_2 (
    .a(demultiplexer_1_out1), .b(demultiplexer_2_out1), .eq(comparator_2_eq), .lt(comparator_2_lt));  // open: gt
  or or_2 (or_2_out, Addi, Slli, Slti, Xori, Srli, Ori, Andi, Lui, Lw, Lw, Lh, Sw, Beq, Blt, Bltu, Jal, Jalr);
  Multiplexer multiplexer_6 (.in0(1'b0), .in1(1'b1), .out(RegWEn), .sel(or_3_out));  // open: en
  or or_3 (or_3_out, Add, Mul, NegSel, Sll, MulH, Slt, Xor, Div, Srl, Or, Rem, And, Addi, Slli, Slti, Xori, Srli, Ori, Andi, Lui, Lb, Lw, Lh, Jal, Jalr);
  Multiplexer multiplexer_7 (.in0(comparator_1_eq), .in1(comparator_2_eq), .out(brEQ), .sel(Bltu));  // open: en
  Multiplexer multiplexer_8 (.in0(comparator_1_lt), .in1(comparator_2_lt), .out(brLT), .sel(Bltu));  // open: en
  not not_49 (addiPCSel, Addi);
  not not_50 (addiASel, Addi);
  assign bit_extender_19_out = {{3{1'b0}}, Addi};  // Bit_Extender bit_extender_19
  not not_51 (addiMemRW, Addi);
  assign addiWBSel = {{1{1'b0}}, Addi};  // Bit_Extender bit_extender_20
  not not_52 (not_52_out, Addi);
  not not_53 (not_53_out, Slli);
  not not_54 (not_54_out, Ori);
  not not_55 (not_55_out, Andi);
  Multiplexer multiplexer_9 (.in0(1'b0), .in1(1'b1), .out(BSel), .sel(or_2_out));  // open: en
  regfile_main main_1 (
    .Read_Register_1__rs1(register_2_q[19:15]), .Read_Register_2__rs2(register_2_q[24:20]),
    .Write_Register__rd(register_2_q[11:7]), .Write_Data(multiplexer_29_out), .Write_Enable(RegWEn),
    .Clock(CLOCK), .Read_Data_1(R1), .Read_Data_2(R2), .s1_Value(s1_Value), .t0_Value(t0_Value),
    .t1_Value(t1_Value), .a0_Value(a0_Value), .s0_Value(s0_Value), .ra_Value(ra_Value), .sp_Value(sp_Value));
  and and_4 (and_4_out, not_52_out, Addi);
  not not_56 (slliPCSel, Slli);
  not not_57 (slliASel, Slli);
  not not_58 (slliMemRW, Slli);
  assign slliWBSel = {{1{1'b0}}, Slli};  // Bit_Extender bit_extender_21
  not not_59 (sltiPCSel, Slti);
  not not_60 (sltiASel, Slti);
  not not_61 (sltiMemRW, Slti);
  assign sltiWBSel = {{1{1'b0}}, Slti};  // Bit_Extender bit_extender_22
  not not_62 (not_62_out, Slti);
  not not_63 (xoriPCSel, Xori);
  not not_64 (xoriASel, Xori);
  not not_65 (xoriMemRW, Xori);
  assign xoriWBSel = {{1{1'b0}}, Xori};  // Bit_Extender bit_extender_23
  not not_66 (not_66_out, Xori);
  not not_67 (srliPCSel, Srli);
  not not_68 (srliASel, Srli);
  not not_69 (srliMemRW, Srli);
  assign srliWBSel = {{1{1'b0}}, Srli};  // Bit_Extender bit_extender_24
  not not_70 (not_70_out, Srli);
  not not_71 (oriPCSel, Ori);
  not not_72 (oriASel, Ori);
  not not_73 (oriMemRW, Ori);
  assign oriWBSel = {{1{1'b0}}, Ori};  // Bit_Extender bit_extender_25
  not not_74 (andiPCSel, Andi);
  not not_75 (andiASel, Andi);
  not not_76 (andiMemRW, Andi);
  assign andiWBSel = {{1{1'b0}}, Andi};  // Bit_Extender bit_extender_26
  or or_4 (or_4_out, Jal, Jalr);
  Shifter #(.width(4)) shifter_6 (.in(bit_extender_19_out), .\dist (2'b01), .out(addiALUSel));
  assign addiImmSel = {{2{1'b0}}, and_4_out};  // Bit_Extender bit_extender_27
  and and_5 (and_5_out, not_53_out, Slli);
  assign slliImmSel = {{2{1'b0}}, and_5_out};  // Bit_Extender bit_extender_28
  and and_6 (and_6_out, not_62_out, Slti);
  and and_7 (and_7_out, not_66_out, Xori);
  and and_8 (and_8_out, not_70_out, Srli);
  and and_9 (and_9_out, not_54_out, Ori);
  assign andiImmSel = {{2{1'b0}}, and_10_out};  // Bit_Extender bit_extender_29
  and and_10 (and_10_out, not_55_out, Andi);
  assign bit_extender_30_out = {{3{1'b0}}, Lui};  // Bit_Extender bit_extender_30
  not not_77 (LuiPCSel, Lui);
  Multiplexer #(.width(2)) multiplexer_10 (
    .in0(2'b00), .in1(2'b01), .out(multiplexer_10_out), .sel(not_78_out));  // open: en
  not not_78 (not_78_out, or_4_out);
  Multiplexer multiplexer_11 (.in0(1'b0), .in1(1'b1), .out(ASel), .sel(or_5_out));  // open: en
  or or_5 (or_5_out, Beq, Blt, Bltu, Jal);
  Multiplexer #(.width(32)) multiplexer_12 (
    .in0(R1), .in1(shifter_7_out), .out(multiplexer_12_out), .sel(Jalr));  // open: en
  Shifter #(.width(32), .shift("ar")) shifter_7 (.in(R1), .\dist (5'b00010), .out(shifter_7_out));
  Multiplexer #(.width(32)) multiplexer_13 (.in0(R2), .in1(immGen), .out(multiplexer_13_out), .sel(BSel));  // open: en
  assign sltiImmSel = {{2{1'b0}}, and_6_out};  // Bit_Extender bit_extender_31
  assign xoriImmSel = {{2{1'b0}}, and_7_out};  // Bit_Extender bit_extender_32
  assign srliImmSel = {{2{1'b0}}, and_8_out};  // Bit_Extender bit_extender_33
  assign oriImmSel = {{2{1'b0}}, and_9_out};  // Bit_Extender bit_extender_34
  not not_79 (LuiASel, Lui);
  not not_80 (LuiMemRW, Lui);
  assign LuiWBSel = {{1{1'b0}}, Lui};  // Bit_Extender bit_extender_35
  Multiplexer #(.width(2)) multiplexer_14 (
    .in0(2'b10), .in1(multiplexer_10_out), .out(WBSel), .sel(not_81_out));  // open: en
  not not_81 (not_81_out, or_6_out);
  or or_6 (or_6_out, Lh, Lw, Lb);
  Multiplexer #(.width(32)) multiplexer_15 (
    .in0(multiplexer_12_out), .in1(prevPC), .out(multiplexer_15_out), .sel(ASel));  // open: en
  Negator #(.width(32)) negator_1 (.in(multiplexer_13_out), .out(negator_1_out));
  control_unit Control_Unit (
    .Instruction(register_2_q), .brEQ(brEQ), .brLT(brLT), .JALRtype(Jalr), .JALtype(Jal), .LUItype(Lui),
    .BLTUtype(Bltu), .BLTtype(Blt), .BEQtype(Beq), .SWtype(Sw), .ANDItype(Andi), .ORItype(Ori),
    .SRLItype(Srli), .XORItype(Xori), .SLTItype(Slti), .SLLItype(Slli), .ADDItype(Addi), .LWtype(Lw),
    .LHtype(Lh), .LBtype(Lb), .ANDtype(And), .REMtype(Rem), .ORtype(Or), .SRLtype(Srl), .DIVtype(Div),
    .XORtype(Xor), .SLTtype(Slt), .MULHtype(MulH), .SLLtype(Sll), .SUBtype(NegSel), .MULtype(Mul),
    .ADDtype(Add));  // open: brEQ_2, brLT_2
  Shifter #(.width(4)) shifter_8 (.in(bit_extender_30_out), .\dist (2'b01), .out(LuiALUSel));
  Multiplexer #(.width(4)) multiplexer_16 (
    .in0(4'b0010), .in1(4'b1010), .out(multiplexer_16_out), .sel(Rem));  // open: en
  Multiplexer #(.width(32)) multiplexer_17 (
    .in0(multiplexer_15_out), .in1({32{1'b0}}), .out(multiplexer_17_out), .sel(Lui));  // open: en
  alu_main main_2 (
    .Switch(ALUSel), .X(multiplexer_17_out), .Result(main_2_result), .Y(multiplexer_18_out));  // open: Equal
  Multiplexer #(.width(32)) multiplexer_18 (
    .in0(multiplexer_13_out), .in1(negator_1_out), .out(multiplexer_18_out), .sel(NegSel));  // open: en
  Multiplexer multiplexer_19 (.in0(1'b0), .in1(1'b1), .out(MemRW), .sel(Sw));  // open: en
  Multiplexer #(.width(4)) multiplexer_20 (
    .in0(multiplexer_16_out), .in1(4'b1001), .out(multiplexer_20_out), .sel(Div));  // open: en
  not not_82 (lbPCSel, Lb);
  not not_83 (lbASel, Lb);
  not not_84 (lbMemRW, Lb);
  not not_85 (not_85_out, Lb);
  not not_86 (lwPCSel, Lw);
  not not_87 (lwASel, Lw);
  not not_88 (lwMemRW, Lw);
  not not_89 (not_89_out, Lw);
  Multiplexer #(.width(4)) multiplexer_21 (
    .in0(multiplexer_20_out), .in1(4'b1000), .out(multiplexer_21_out), .sel(MulH));  // open: en
  Shifter #(.width(32)) shifter_9 (.in(FETCH_ADDRESS), .\dist (5'b00010), .out(shifter_9_out));
  // mem_main MEM: pin names not known; wires that end beside it: MEM_p1, MEM_p2, MEM_p2, MEM_p4, main_2_result, R2, MemRW, MEM_p4, CLOCK, MEM_p10, Load
  and and_11 (and_11_out, not_85_out, Lb);
  not not_90 (lhPCSel, Lh);
  not not_91 (lhASel, Lh);
  not not_92 (lhMemRW, Lh);
  not not_93 (not_93_out, Lh);
  not not_94 (SwPCSel, Sw);
  not not_95 (SwASel, Sw);
  assign bit_extender_36_out = {{3{1'b0}}, Sw};  // Bit_Extender bit_extender_36
  not not_96 (SwRegWEn, Sw);
  assign SwWBSel = {{1{1'b0}}, Sw};  // Bit_Extender bit_extender_37
  assign bit_extender_38_out = {{3{1'b0}}, Jal};  // Bit_Extender bit_extender_38
  not not_97 (JalMemRW, Jal);
  assign bit_extender_39_out = {{3{1'b0}}, Jalr};  // Bit_Extender bit_extender_39
  not not_98 (JalrMemRW, Jalr);
  Multiplexer #(.width(3)) multiplexer_22 (
    .in0(3'b000), .in1(3'b100), .out(multiplexer_22_out), .sel(Jal));  // open: en
  Multiplexer #(.width(4)) multiplexer_23 (
    .in0(multiplexer_21_out), .in1(4'b0111), .out(multiplexer_23_out), .sel(Mul));  // open: en
  Multiplexer #(.width(4)) multiplexer_24 (
    .in0(multiplexer_23_out), .in1(4'b0110), .out(multiplexer_24_out), .sel(or_7_out));  // open: en
  or or_7 (or_7_out, Slti, Slt);
  assign bit_extender_40_out = {{24{1'b0}}, Load[7:0]};  // Bit_Extender bit_extender_40
  Multiplexer #(.width(32)) multiplexer_25 (
    .in0(bit_extender_40_out), .in1(bit_extender_41_out), .out(multiplexer_25_out), .sel(Lh));  // open: en
  assign bit_extender_41_out = {{16{1'b0}}, Load[15:0]};  // Bit_Extender bit_extender_41
  assign bit_extender_42_out = {{3{1'b0}}, Lb};  // Bit_Extender bit_extender_42
  assign lbImmSel = {{2{1'b0}}, and_11_out};  // Bit_Extender bit_extender_43
  assign bit_extender_44_out = {{3{1'b0}}, Lw};  // Bit_Extender bit_extender_44
  and and_12 (and_12_out, not_89_out, Lw);
  and and_13 (and_13_out, not_93_out, Lh);
  Shifter #(.width(4)) shifter_10 (.in(bit_extender_36_out), .\dist (2'b01), .out(SwALUSel));
  assign bit_extender_45_out = {{3{1'b0}}, Beq};  // Bit_Extender bit_extender_45
  not not_99 (BeqMemRW, Beq);
  not not_100 (BeqRegWEn, Beq);
  assign BeqWBSel = {{1{1'b0}}, Beq};  // Bit_Extender bit_extender_46
  assign bit_extender_47_out = {{3{1'b0}}, Blt};  // Bit_Extender bit_extender_47
  assign BltWBSel = {{1{1'b0}}, Blt};  // Bit_Extender bit_extender_48
  Shifter #(.width(4)) shifter_11 (.in(bit_extender_38_out), .\dist (2'b01), .out(JalALUSel));
  not not_101 (not_101_out, Jalr);
  not not_102 (JalrASel, Jalr);
  Shifter #(.width(4)) shifter_12 (.in(bit_extender_39_out), .\dist (2'b01), .out(JalrALUSel));
  Multiplexer #(.width(3)) multiplexer_26 (
    .in0(multiplexer_22_out), .in1(3'b011), .out(multiplexer_26_out), .sel(Lui));  // open: en
  Multiplexer #(.width(3)) multiplexer_27 (
    .in0(multiplexer_26_out), .in1(3'b010), .out(multiplexer_27_out), .sel(or_8_out));  // open: en
  or or_8 (or_8_out, Beq, Bltu, Blt);
  Multiplexer #(.width(4)) multiplexer_28 (
    .in0(multiplexer_24_out), .in1(4'b0101), .out(multiplexer_28_out), .sel(or_9_out));  // open: en
  or or_9 (or_9_out, Xor, Xori);
  Multiplexer #(.select(2), .width(32)) multiplexer_29 (
    .in0(shifter_9_out), .in1(main_2_result), .in2(LoadOut), .out(multiplexer_29_out), .sel(WBSel));  // open: in3, en
  Multiplexer #(.width(32)) multiplexer_30 (.in0(multiplexer_25_out), .in1(Load), .out(LoadOut), .sel(Lw));  // open: en
  Shifter #(.width(4)) shifter_13 (.in(bit_extender_42_out), .\dist (2'b01), .out(lbALUSel));
  assign lwImmSel = {{2{1'b0}}, and_12_out};  // Bit_Extender bit_extender_49
  assign bit_extender_50_out = {{3{1'b0}}, Lh};  // Bit_Extender bit_extender_50
  assign lhImmSel = {{2{1'b0}}, and_13_out};  // Bit_Extender bit_extender_51
  Shifter #(.width(4)) shifter_14 (.in(bit_extender_45_out), .\dist (2'b01), .out(BeqALUSel));
  not not_103 (BltMemRW, Blt);
  not not_104 (BltRegWEn, Blt);
  assign bit_extender_52_out = {{3{1'b0}}, Bltu};  // Bit_Extender bit_extender_52
  not not_105 (BltuMemRW, Bltu);
  not not_106 (BltuRegWEn, Bltu);
  assign BltuWBSel = {{1{1'b0}}, Bltu};  // Bit_Extender bit_extender_53
  and and_14 (and_14_out, not_101_out, Jalr);
  Multiplexer #(.width(3)) multiplexer_31 (.in0(multiplexer_27_out), .in1(3'b001), .out(ImmSel), .sel(Sw));  // open: en
  Multiplexer #(.width(4)) multiplexer_32 (
    .in0(multiplexer_28_out), .in1(4'b0100), .out(multiplexer_32_out), .sel(or_11_out));  // open: en
  or or_10 (or_10_out, And, Andi);
  or or_11 (or_11_out, Or, Ori);
  Shifter #(.width(4)) shifter_15 (.in(bit_extender_44_out), .\dist (2'b01), .out(lwALUSel));
  Shifter #(.width(4)) shifter_16 (.in(bit_extender_50_out), .\dist (2'b01), .out(lhALUSel));
  Shifter #(.width(4)) shifter_17 (.in(bit_extender_47_out), .\dist (2'b01), .out(BltALUSel));
  Shifter #(.width(4)) shifter_18 (.in(bit_extender_52_out), .\dist (2'b01), .out(BltuALUSel));
  assign JalrImmSel = {{2{1'b0}}, and_14_out};  // Bit_Extender bit_extender_54
  Multiplexer #(.width(4)) multiplexer_33 (
    .in0(multiplexer_32_out), .in1(4'b0011), .out(multiplexer_33_out), .sel(or_10_out));  // open: en
  Multiplexer #(.width(4)) multiplexer_34 (
    .in0(multiplexer_33_out), .in1(4'b0001), .out(multiplexer_34_out), .sel(or_12_out));  // open: en
  or or_12 (or_12_out, Srl, Srli);
  Multiplexer #(.width(4)) multiplexer_35 (
    .in0(multiplexer_34_out), .in1(4'b0000), .out(ALUSel), .sel(or_13_out));  // open: en
  or or_13 (or_13_out, Sll, Slli);

  // Other names for the same wires on the sheet: a0[31:0] = a0_Value; addiBSel = Addi; addiRegWEn = Addi;
  //   addRegWEn = Add; andiALUSel = Andi; andiBSel = Andi; andiRegWEn = Andi; andALUSel = And; andRegWEn = And;
  //   BeqASel = Beq; BeqBSel = Beq; BeqiImmSel = Beq; BltASel = Blt; BltBSel = Blt; BltiImmSel = Blt; BltuASel = Bltu;
  //   BltuBSel = Bltu; BltuiImmSel = Bltu; clk = CLOCK; divALUSel = Div; divRegWEn = Div;
  //   fetch_addr[31:0] = FETCH_ADDRESS; PCHold[31:0] = FETCH_ADDRESS; JalASel = Jal; JalBSel = Jal; JaliImmSel = Jal;
  //   JalPCSel = Jal; JalRegWEn = Jal; JalWBSel = Jal; JalrBSel = Jalr; JalrPCSel = Jalr; JalrRegWEn = Jalr;
  //   JalrWBSel = Jalr; lbBSel = Lb; lbRegWEn = Lb; lbWBSel = Lb; lhBSel = Lh; lhRegWEn = Lh; lhWBSel = Lh;
  //   LuiBSel = Lui; LuiiImmSel = Lui; LuiRegWEn = Lui; LuiSel = Lui; lwBSel = Lw; lwRegWEn = Lw; lwWBSel = Lw;
  //   mulhALUSel = MulH; mulhRegWEn = MulH; mulALUSel = Mul; mulRegWEn = Mul; oriALUSel = Ori; oriBSel = Ori;
  //   oriRegWEn = Ori; orALUSel = Or; orRegWEn = Or; ra[31:0] = ra_Value; remALUSel = Rem; remRegWEn = Rem;
  //   s0[31:0] = s0_Value; s1[31:0] = s1_Value; slliALUSel = Slli; slliBSel = Slli; slliRegWEn = Slli;
  //   sllALUSel = Sll; sllRegWEn = Sll; sltiALUSel = Slti; sltiBSel = Slti; sltiRegWEn = Slti; sltALUSel = Slt;
  //   sltRegWEn = Slt; sp[31:0] = sp_Value; srliALUSel = Srli; srliBSel = Srli; srliRegWEn = Srli; srlALUSel = Srl;
  //   srlRegWEn = Srl; Sub = NegSel; subRegWEn = NegSel; SwBSel = Sw; swImmSel = Sw; SwMemRW = Sw;
  //   t0[31:0] = t0_Value; t1[31:0] = t1_Value; xoriALUSel = Xori; xoriBSel = Xori; xoriRegWEn = Xori;
  //   xorALUSel = Xor; xorRegWEn = Xor

  // Notes on the sheet:
  //   Output
  //   These are outputs/inputs from run.circ
  //   Inputs
  //   These are DEBUG/TEST outputs from your circuit.
endmodule

module control_unit (
  input  [31:0] Instruction,
  input  brEQ,
  input  brLT,
  output JALRtype,
  output JALtype,
  output LUItype,
  output BLTUtype,
  output BLTtype,
  output BEQtype,
  output SWtype,
  output ANDItype,
  output ORItype,
  output SRLItype,
  output XORItype,
  output SLTItype,
  output SLLItype,
  output ADDItype,
  output LWtype,
  output LHtype,
  output LBtype,
  output ANDtype,
  output REMtype,
  output ORtype,
  output SRLtype,
  output DIVtype,
  output XORtype,
  output SLTtype,
  output MULHtype,
  output SLLtype,
  output SUBtype,
  output MULtype,
  output ADDtype,
  output brEQ_2,
  output brLT_2
);

  wire demultiplexer_1_out0, demultiplexer_1_out1, demultiplexer_2_out0, demultiplexer_3_out0,
       demultiplexer_4_out0, demultiplexer_4_out1, demultiplexer_5_out1, demultiplexer_6_out0,
       demultiplexer_9_out1, demultiplexer_11_out0, demultiplexer_11_out1, demultiplexer_12_out0,
       demultiplexer_12_out1, demultiplexer_13_out0, demultiplexer_13_out1, demultiplexer_16_out0,
       demultiplexer_16_out1, demultiplexer_17_out0, demultiplexer_17_out1, demultiplexer_18_out0,
       demultiplexer_18_out1, demultiplexer_20_out0, demultiplexer_21_out0, demultiplexer_21_out1,
       demultiplexer_22_out0, demultiplexer_22_out1, demultiplexer_23_out0, demultiplexer_23_out1,
       demultiplexer_24_out0, demultiplexer_24_out1, demultiplexer_26_out0, Itype, LoadItype, Rtype;

  Demultiplexer demultiplexer_1 (
    .out0(demultiplexer_1_out0), .out1(demultiplexer_1_out1), .in(1'b1), .sel(Instruction[6]));  // open: en
  Demultiplexer demultiplexer_2 (
    .out0(demultiplexer_2_out0), .out1(JALtype), .in(demultiplexer_1_out1), .sel(Instruction[3]));  // open: en
  Demultiplexer demultiplexer_3 (
    .out0(demultiplexer_3_out0), .out1(Itype), .in(demultiplexer_4_out0), .sel(Instruction[4]));  // open: en
  Demultiplexer demultiplexer_4 (
    .out0(demultiplexer_4_out0), .out1(demultiplexer_4_out1), .in(demultiplexer_1_out0), .sel(Instruction[5]));  // open: en
  Demultiplexer demultiplexer_5 (
    .out0(SWtype), .out1(demultiplexer_5_out1), .in(demultiplexer_4_out1), .sel(Instruction[4]));  // open: en
  Demultiplexer demultiplexer_6 (
    .out0(demultiplexer_6_out0), .out1(JALRtype), .in(demultiplexer_2_out0), .sel(Instruction[2]));  // open: en
  Demultiplexer demultiplexer_7 (
    .out0(Rtype), .out1(LUItype), .in(demultiplexer_5_out1), .sel(Instruction[2]));  // open: en
  Demultiplexer demultiplexer_8 (.out1(LoadItype), .in(demultiplexer_3_out0), .sel(Instruction[1]));  // open: out0, en
  Demultiplexer demultiplexer_9 (
    .out0(BEQtype), .out1(demultiplexer_9_out1), .in(demultiplexer_6_out0), .sel(Instruction[14]));  // open: en
  Demultiplexer demultiplexer_10 (
    .out0(BLTtype), .out1(BLTUtype), .in(demultiplexer_9_out1), .sel(Instruction[13]));  // open: en
  Demultiplexer demultiplexer_11 (
    .out0(demultiplexer_11_out0), .out1(demultiplexer_11_out1), .in(demultiplexer_12_out0),
    .sel(Instruction[13]));  // open: en
  Demultiplexer demultiplexer_12 (
    .out0(demultiplexer_12_out0), .out1(demultiplexer_12_out1), .in(Itype), .sel(Instruction[14]));  // open: en
  Demultiplexer demultiplexer_13 (
    .out0(demultiplexer_13_out0), .out1(demultiplexer_13_out1), .in(demultiplexer_12_out1),
    .sel(Instruction[13]));  // open: en
  Demultiplexer demultiplexer_14 (
    .out0(ADDItype), .out1(SLLItype), .in(demultiplexer_11_out0), .sel(Instruction[12]));  // open: en
  Demultiplexer demultiplexer_15 (
    .out0(XORItype), .out1(SRLItype), .in(demultiplexer_13_out0), .sel(Instruction[12]));  // open: en
  Demultiplexer demultiplexer_16 (
    .out0(demultiplexer_16_out0), .out1(demultiplexer_16_out1), .in(demultiplexer_17_out0),
    .sel(Instruction[13]));  // open: en
  Demultiplexer demultiplexer_17 (
    .out0(demultiplexer_17_out0), .out1(demultiplexer_17_out1), .in(Rtype), .sel(Instruction[14]));  // open: en
  Demultiplexer demultiplexer_18 (
    .out0(demultiplexer_18_out0), .out1(demultiplexer_18_out1), .in(demultiplexer_17_out1),
    .sel(Instruction[13]));  // open: en
  Demultiplexer demultiplexer_19 (
    .out0(SLTItype), .in(demultiplexer_11_out1), .sel(Instruction[12]));  // open: out1, en
  Demultiplexer demultiplexer_20 (
    .out0(demultiplexer_20_out0), .out1(LWtype), .in(LoadItype), .sel(Instruction[13]));  // open: en
  Demultiplexer demultiplexer_21 (
    .out0(demultiplexer_21_out0), .out1(demultiplexer_21_out1), .in(demultiplexer_16_out0),
    .sel(Instruction[12]));  // open: en
  Demultiplexer demultiplexer_22 (
    .out0(demultiplexer_22_out0), .out1(demultiplexer_22_out1), .in(demultiplexer_16_out1),
    .sel(Instruction[12]));  // open: en
  Demultiplexer demultiplexer_23 (
    .out0(demultiplexer_23_out0), .out1(demultiplexer_23_out1), .in(demultiplexer_18_out0),
    .sel(Instruction[12]));  // open: en
  Demultiplexer demultiplexer_24 (
    .out0(demultiplexer_24_out0), .out1(demultiplexer_24_out1), .in(demultiplexer_18_out1),
    .sel(Instruction[12]));  // open: en
  Demultiplexer demultiplexer_25 (
    .out0(ORItype), .out1(ANDItype), .in(demultiplexer_13_out1), .sel(Instruction[12]));  // open: en
  Demultiplexer demultiplexer_26 (
    .out0(demultiplexer_26_out0), .out1(SUBtype), .in(demultiplexer_21_out0), .sel(Instruction[30]));  // open: en
  Demultiplexer demultiplexer_27 (
    .out0(SLLtype), .out1(MULHtype), .in(demultiplexer_21_out1), .sel(Instruction[25]));  // open: en
  Demultiplexer demultiplexer_28 (.out0(SLTtype), .in(demultiplexer_22_out0), .sel(Instruction[25]));  // open: out1, en
  Demultiplexer demultiplexer_29 (.in(demultiplexer_22_out1), .sel(Instruction[25]));  // open: out0, out1, en
  Demultiplexer demultiplexer_30 (
    .out0(XORtype), .out1(DIVtype), .in(demultiplexer_23_out0), .sel(Instruction[25]));  // open: en
  Demultiplexer demultiplexer_31 (.out0(SRLtype), .in(demultiplexer_23_out1), .sel(Instruction[25]));  // open: out1, en
  Demultiplexer demultiplexer_32 (
    .out0(ORtype), .out1(REMtype), .in(demultiplexer_24_out0), .sel(Instruction[25]));  // open: en
  Demultiplexer demultiplexer_33 (.out0(ANDtype), .in(demultiplexer_24_out1), .sel(Instruction[25]));  // open: out1, en
  Demultiplexer demultiplexer_34 (
    .out0(LBtype), .out1(LHtype), .in(demultiplexer_20_out0), .sel(Instruction[12]));  // open: en
  Demultiplexer demultiplexer_35 (
    .out0(ADDtype), .out1(MULtype), .in(demultiplexer_26_out0), .sel(Instruction[25]));  // open: en

  assign brEQ_2 = brEQ;
  assign brLT_2 = brLT;

  // Other names for the same wires on the sheet: Op1 = Instruction[1]; Op2 = Instruction[2]; Op3 = Instruction[3];
  //   Op4 = Instruction[4]; Op5 = Instruction[5]; Op6 = Instruction[6]; Func3_12 = Instruction[12];
  //   Func3_13 = Instruction[13]; Func3_14 = Instruction[14]; Func7_25 = Instruction[25]; Func7_30 = Instruction[30]

  // Notes on the sheet:
  //   ITypes
  //   UJTypes
  //   UTypes
  //   SBTypes
  //   STypes
  //   ITypes
  //   RTypes
endmodule
